// Logisim project cpu.circ as structural Verilog: 12 circuits, main circuit main
module main (
);

  wire decoder_1_out0, decoder_1_out1, decoder_1_out3, or_1_out, or_2_out, ram_1_p6;
  wire [1:0] sips_1_accessamt;
  wire [7:0] undriven, undriven_2, undriven_3, undriven_4;
  wire [23:0] bit_extender_1_out;
  wire [31:0] sips_1_address, sips_1_dataout;

  Decoder #(.enable("false"), .select(2)) decoder_1 (
    .out0(decoder_1_out0), .out1(decoder_1_out1), .out3(decoder_1_out3), .sel(sips_1_accessamt));  // open: out2
  or or_1 (or_1_out, decoder_1_out0, decoder_1_out1, decoder_1_out3);
  or or_2 (or_2_out, decoder_1_out1, decoder_1_out3);
  Bit_Extender #(.in_width(32), .out_width(24), .\type ("zero")) bit_extender_1 (
    .in(sips_1_address), .out(bit_extender_1_out));
  // RAM #(.addrWidth(24), .enables("line"), .line("quad"), .misaligned("true"), .\type ("nonvolatile")) ram_1: pin names not known; wires that end beside it: bit_extender_1_out, or_1_out, or_2_out, decoder_1_out3, decoder_1_out3, ram_1_p6
  sips sips_1 (
    .dataIn({undriven_4, undriven_3, undriven_2, undriven}), .address(sips_1_address),
    .accessAmt(sips_1_accessamt), .write(ram_1_p6), .dataOut(sips_1_dataout));  // open: read
endmodule

module sips (
  input  [31:0] dataIn,
  output [31:0] address,
  output [1:0] accessAmt,
  output read,
  output write,
  output [31:0] dataOut
);

  wire and_1_out, and_2_out, and_3_out, and_6_out, buffer_1_out, buffer_2_out, buffer_3_out, buffer_4_out,
       buffer_5_out, buffer_6_out, buffer_7_out, buffer_8_out, buffer_9_out, buffer_10_out, clock_1_out,
       comparator_1_eq, comparator_1_gt, comparator_1_lt, comparator_2_eq, comparator_2_gt, comparator_2_lt,
       comparator_3_eq, decoderer_1_aluop, decoderer_1_branch, decoderer_1_jump, decoderer_1_readsmem,
       decoderer_1_regstore, decoderer_1_usesbrex, decoderer_1_usesimm, decoderer_1_writesmem,
       multiplexer_4_out, not_1_out, not_2_out, not_3_out, not_4_out, or_1_out, or_2_out, or_3_out, or_4_out,
       or_5_out, or_6_out, or_7_out, or_8_out, pull_resistor_4_node, pull_resistor_5_node, stagereg_1_aluop,
       stagereg_1_branch, stagereg_1_jump, stagereg_1_readsmem, stagereg_1_regstore, stagereg_1_usesbrex,
       stagereg_1_usesimm, stagereg_1_writesmem, stagereg_2_aluop, stagereg_2_branch, stagereg_2_jump,
       stagereg_2_readsmem, stagereg_2_regstore, stagereg_2_usesbrex, stagereg_2_usesimm,
       stagereg_2_writesmem, stagereg_3_aluop, stagereg_3_branch, stagereg_3_jump, stagereg_3_readsmem,
       stagereg_3_regstore, stagereg_3_usesbrex, stagereg_3_usesimm, stagereg_3_writesmem, stagereg_4_jump,
       stagereg_4_regstore;
  wire [1:0] bit_extender_3_out, forwarding_unit_1_out_5, forwarding_unit_2_out_5,
       forwarding_unit_big_1_out_6, forwarding_unit_big_2_out_6, pull_resistor_1_node, pull_resistor_2_node,
       pull_resistor_6_node;
  wire [4:0] decoderer_1_arex, decoderer_1_brex, decoderer_1_shout, decoderer_1_trex, stagereg_1_arex,
       stagereg_1_brex, stagereg_1_shout, stagereg_1_trex, stagereg_2_arex, stagereg_2_brex,
       stagereg_2_shout, stagereg_2_trex, stagereg_3_arex, stagereg_3_brex, stagereg_3_shout,
       stagereg_3_trex, stagereg_4_trex;
  wire [5:0] decoderer_1_funcout, decoderer_1_opout, stagereg_1_funcout, stagereg_1_opout,
       stagereg_2_funcout, stagereg_2_opout, stagereg_3_funcout, stagereg_3_opout;
  wire [7:0] stagereg_3_bdata, stagereg_3_bdata_2, stagereg_3_bdata_3, stagereg_3_bdata_4;
  wire [15:0] bit_extender_1_out;
  wire [25:0] bit_extender_2_out;
  wire [31:0] adder_1_out, adder_2_out, adder_3_out, alu_1_out_6, bit_extender_4_out, bit_extender_5_out,
       bit_extender_6_out, bit_extender_7_out, bit_extender_8_out, bit_extender_9_out, decoderer_1_imm,
       decoderer_1_pcout, multiplexer_3_out, multiplexer_5_out, multiplexer_6_out, multiplexer_7_out,
       multiplexer_8_out, multiplexer_9_out, multiplexer_10_out, multiplexer_11_out, multiplexer_12_out,
       multiplexer_14_out, pull_resistor_3_node, register_1_q, register_2_q, regs_1_out_6, regs_1_out_7,
       stagereg_1_opdata, stagereg_1_pcout, stagereg_2_adata, stagereg_2_bdata, stagereg_2_opdata,
       stagereg_2_pcout, stagereg_3_adata, stagereg_3_opdata, stagereg_3_pcout, stagereg_4_opdata,
       stagereg_4_pcout;

  Multiplexer #(.width(32)) multiplexer_1 (.in0(adder_2_out), .in1(register_1_q), .out(address), .sel(not_1_out));
  Multiplexer #(.width(2)) multiplexer_2 (
    .in0(stagereg_3_opout[1:0]), .in1(pull_resistor_1_node), .out(accessAmt), .sel(not_1_out));
  Pull_Resistor #(.pull(1)) pull_resistor_1 (.node(pull_resistor_1_node));
  not not_1 (not_1_out, buffer_1_out);
  buf buffer_1 (buffer_1_out, or_8_out);
  Bit_Extender #(.in_width(32), .\type ("zero")) bit_extender_1 (.in(dataIn), .out(bit_extender_1_out));
  Bit_Extender #(.in_width(32), .out_width(26), .\type ("zero")) bit_extender_2 (.in(dataIn), .out(bit_extender_2_out));
  Adder #(.width(32)) adder_1 (.a(register_1_q), .b(32'h4), .out(adder_1_out));  // open: cin, cout
  Multiplexer #(.width(32)) multiplexer_3 (
    .in0(adder_1_out), .in1({stagereg_1_opdata[29:0], pull_resistor_2_node}), .out(multiplexer_3_out),
    .sel(and_1_out));
  decoderer decoderer_1 (
    .func(dataIn[5:0]), .sh(dataIn[10:6]), .rd(dataIn[15:11]), .rt(dataIn[20:16]), .rs(dataIn[25:21]),
    .op(dataIn[31:26]), .imm16(bit_extender_1_out), .imm26(bit_extender_2_out), .pc(register_1_q),
    .cancelInst(and_1_out), .opOut(decoderer_1_opout), .funcOut(decoderer_1_funcout),
    .shOut(decoderer_1_shout), .trex(decoderer_1_trex), .arex(decoderer_1_arex), .brex(decoderer_1_brex),
    .regStore(decoderer_1_regstore), .jump(decoderer_1_jump), .branch(decoderer_1_branch),
    .usesBRex(decoderer_1_usesbrex), .usesImm(decoderer_1_usesimm), .writesMem(decoderer_1_writesmem),
    .readsMem(decoderer_1_readsmem), .aluOp(decoderer_1_aluop), .imm(decoderer_1_imm),
    .pcOut(decoderer_1_pcout));
  Register #(.width(32)) register_1 (.D(multiplexer_3_out), .Q(register_1_q), .clk(not_2_out));  // open: en, clr
  not not_2 (not_2_out, clock_1_out);
  stageReg stagereg_1 (
    .in_1(decoderer_1_opout), .in_2(decoderer_1_funcout), .in_3(decoderer_1_shout), .in_4(decoderer_1_trex),
    .in_5(decoderer_1_arex), .in_6(decoderer_1_brex), .in_7(decoderer_1_regstore), .in_8(decoderer_1_jump),
    .in_9(decoderer_1_branch), .in_10(decoderer_1_usesbrex), .in_11(decoderer_1_usesimm),
    .in_12(decoderer_1_writesmem), .in_13(decoderer_1_readsmem), .in_14(decoderer_1_aluop),
    .in_15(decoderer_1_imm), .in_16(decoderer_1_pcout), .store(clock_1_out), .opOut(stagereg_1_opout),
    .funcOut(stagereg_1_funcout), .shOut(stagereg_1_shout), .trex(stagereg_1_trex), .arex(stagereg_1_arex),
    .brex(stagereg_1_brex), .regStore(stagereg_1_regstore), .jump(stagereg_1_jump),
    .branch(stagereg_1_branch), .usesBRex(stagereg_1_usesbrex), .usesImm(stagereg_1_usesimm),
    .writesMem(stagereg_1_writesmem), .readsMem(stagereg_1_readsmem), .aluOp(stagereg_1_aluop),
    .opData(stagereg_1_opdata), .pcOut(stagereg_1_pcout));  // open: in_17, in_18, flush, aData, bData
  and and_1 (and_1_out, stagereg_1_jump, or_1_out);
  or or_1 (or_1_out, ~stagereg_1_branch, and_2_out);  // OR_Gate
  Clock clock_1 (.out(clock_1_out));
  Regs regs_1 (
    .in_1(stagereg_4_trex), .in_2(stagereg_1_arex), .in_3(stagereg_1_brex), .in_4(multiplexer_14_out),
    .in_5(and_6_out), .out_6(regs_1_out_6), .out_7(regs_1_out_7));
  Pull_Resistor pull_resistor_2 (.node({stagereg_1_opdata[29:0], pull_resistor_2_node}));
  Pull_Resistor pull_resistor_3 (.node(pull_resistor_3_node));
  Multiplexer #(.select(2)) multiplexer_4 (
    .in0(comparator_1_eq), .in1(or_2_out), .in2(or_3_out), .in3(comparator_2_gt), .out(multiplexer_4_out),
    .sel(bit_extender_3_out));
  and and_2 (and_2_out, multiplexer_4_out, stagereg_1_branch);
  Multiplexer #(.width(32)) multiplexer_5 (
    .in0(stagereg_1_opdata), .in1(regs_1_out_7), .out(multiplexer_5_out), .sel(stagereg_1_usesbrex));
  or or_2 (or_2_out, comparator_1_gt, comparator_1_lt);
  Comparator #(.width(32)) comparator_1 (
    .a(multiplexer_6_out), .b(multiplexer_7_out), .gt(comparator_1_gt), .eq(comparator_1_eq),
    .lt(comparator_1_lt));
  Comparator #(.width(32)) comparator_2 (
    .a(multiplexer_6_out), .b(pull_resistor_3_node), .gt(comparator_2_gt), .eq(comparator_2_eq),
    .lt(comparator_2_lt));
  Bit_Extender #(.in_width(6), .out_width(2), .\type ("zero")) bit_extender_3 (
    .in(stagereg_1_opout), .out(bit_extender_3_out));
  or or_3 (or_3_out, comparator_2_lt, comparator_2_eq);
  Multiplexer #(.select(2), .width(32)) multiplexer_6 (
    .in0(multiplexer_5_out), .in1(multiplexer_10_out), .in2(stagereg_4_pcout), .in3(register_2_q),
    .out(multiplexer_6_out), .sel(forwarding_unit_big_2_out_6));
  Multiplexer #(.select(2), .width(32)) multiplexer_7 (
    .in0(regs_1_out_6), .in1(multiplexer_10_out), .in2(stagereg_4_pcout), .in3(register_2_q),
    .out(multiplexer_7_out), .sel(forwarding_unit_big_1_out_6));
  forwarding_unit_big forwarding_unit_big_1 (
    .out_6(forwarding_unit_big_1_out_6), .s(stagereg_1_arex), .t1(stagereg_2_trex), .t2(stagereg_3_trex),
    .t3(stagereg_4_trex), .in_5(pull_resistor_4_node));
  or or_4 (or_4_out, stagereg_2_regstore, stagereg_3_regstore, stagereg_4_regstore);
  Pull_Resistor pull_resistor_4 (.node(pull_resistor_4_node));
  assign pull_resistor_4_node = stagereg_1_branch ? or_4_out : 1'bz;  // Controlled_Buffer controlled_buffer_1
  forwarding_unit_big forwarding_unit_big_2 (
    .out_6(forwarding_unit_big_2_out_6), .s(stagereg_1_brex), .t1(stagereg_2_trex), .t2(stagereg_3_trex),
    .t3(stagereg_4_trex), .in_5(pull_resistor_5_node));
  stageReg stagereg_2 (
    .in_1(stagereg_1_opout), .in_2(stagereg_1_funcout), .in_3(stagereg_1_shout), .in_4(stagereg_1_trex),
    .in_5(stagereg_1_arex), .in_6(stagereg_1_brex), .in_7(stagereg_1_regstore), .in_8(stagereg_1_jump),
    .in_9(stagereg_1_branch), .in_10(stagereg_1_usesbrex), .in_11(stagereg_1_usesimm),
    .in_12(stagereg_1_writesmem), .in_13(stagereg_1_readsmem), .in_14(stagereg_1_aluop),
    .in_15(stagereg_1_opdata), .in_16(stagereg_1_pcout), .in_17(regs_1_out_6), .in_18(multiplexer_5_out),
    .store(clock_1_out), .opOut(stagereg_2_opout), .funcOut(stagereg_2_funcout), .shOut(stagereg_2_shout),
    .trex(stagereg_2_trex), .arex(stagereg_2_arex), .brex(stagereg_2_brex), .regStore(stagereg_2_regstore),
    .jump(stagereg_2_jump), .branch(stagereg_2_branch), .usesBRex(stagereg_2_usesbrex),
    .usesImm(stagereg_2_usesimm), .writesMem(stagereg_2_writesmem), .readsMem(stagereg_2_readsmem),
    .aluOp(stagereg_2_aluop), .opData(stagereg_2_opdata), .pcOut(stagereg_2_pcout), .aData(stagereg_2_adata),
    .bData(stagereg_2_bdata));  // open: flush
  or or_5 (or_5_out, stagereg_2_regstore, stagereg_3_regstore, stagereg_4_regstore);
  Pull_Resistor pull_resistor_5 (.node(pull_resistor_5_node));
  assign pull_resistor_5_node = stagereg_1_branch ? or_5_out : 1'bz;  // Controlled_Buffer controlled_buffer_2
  Pull_Resistor pull_resistor_6 (.node(pull_resistor_6_node));
  assign pull_resistor_6_node = not_3_out ? forwarding_unit_1_out_5 : 2'bz;  // Controlled_Buffer controlled_buffer_3
  not not_3 (not_3_out, stagereg_2_usesimm);
  Multiplexer #(.select(2), .width(32)) multiplexer_8 (
    .in0(stagereg_2_adata), .in1(register_2_q), .in2(stagereg_4_pcout), .out(multiplexer_8_out),
    .sel(forwarding_unit_2_out_5));  // open: in3
  Multiplexer #(.select(2), .width(32)) multiplexer_9 (
    .in0(stagereg_2_bdata), .in1(register_2_q), .in2(stagereg_4_pcout), .out(multiplexer_9_out),
    .sel(pull_resistor_6_node));  // open: in3
  forwarding_unit forwarding_unit_1 (
    .out_5(forwarding_unit_1_out_5), .s(stagereg_2_brex), .t1(stagereg_3_trex), .t2(stagereg_4_trex),
    .in_4(or_6_out));
  Comparator #(.width(6)) comparator_3 (.a(stagereg_2_opout), .b(6'b001111), .eq(comparator_3_eq));  // open: gt, lt
  alu alu_1 (
    .in_1(multiplexer_8_out), .in_2(multiplexer_9_out), .in_3(stagereg_2_funcout), .in_4(stagereg_2_shout),
    .in_5(clock_1_out), .out_6(alu_1_out_6));  // open: out_7, out_8
  or or_6 (or_6_out, stagereg_3_regstore, stagereg_4_regstore);
  forwarding_unit forwarding_unit_2 (
    .out_5(forwarding_unit_2_out_5), .s(stagereg_2_arex), .t1(stagereg_3_trex), .t2(stagereg_4_trex),
    .in_4(or_7_out));
  stageReg stagereg_3 (
    .in_1(stagereg_2_opout), .in_2(stagereg_2_funcout), .in_3(stagereg_2_shout), .in_4(stagereg_2_trex),
    .in_5(stagereg_2_arex), .in_6(stagereg_2_brex), .in_7(stagereg_2_regstore), .in_8(stagereg_2_jump),
    .in_9(stagereg_2_branch), .in_10(stagereg_2_usesbrex), .in_11(stagereg_2_usesimm),
    .in_12(stagereg_2_writesmem), .in_13(stagereg_2_readsmem), .in_14(stagereg_2_aluop),
    .in_15(multiplexer_10_out), .in_16(stagereg_2_pcout), .in_17(multiplexer_8_out),
    .in_18(multiplexer_9_out), .store(clock_1_out), .opOut(stagereg_3_opout), .funcOut(stagereg_3_funcout),
    .shOut(stagereg_3_shout), .trex(stagereg_3_trex), .arex(stagereg_3_arex), .brex(stagereg_3_brex),
    .regStore(stagereg_3_regstore), .jump(stagereg_3_jump), .branch(stagereg_3_branch),
    .usesBRex(stagereg_3_usesbrex), .usesImm(stagereg_3_usesimm), .writesMem(stagereg_3_writesmem),
    .readsMem(stagereg_3_readsmem), .aluOp(stagereg_3_aluop), .opData(stagereg_3_opdata),
    .pcOut(stagereg_3_pcout), .aData(stagereg_3_adata),
    .bData({stagereg_3_bdata_4, stagereg_3_bdata_3, stagereg_3_bdata_2, stagereg_3_bdata}));  // open: flush
  and and_3 (and_3_out, ~comparator_3_eq, stagereg_2_aluop);  // AND_Gate
  Multiplexer #(.width(32)) multiplexer_10 (
    .in0(stagereg_2_opdata), .in1(alu_1_out_6), .out(multiplexer_10_out), .sel(and_3_out));
  or or_7 (or_7_out, stagereg_3_regstore, stagereg_4_regstore);
  Adder #(.width(32)) adder_2 (.a(stagereg_3_opdata), .b(stagereg_3_adata), .out(adder_2_out));  // open: cin, cout
  assign bit_extender_4_out = {{24{dataIn[7]}}, dataIn[7:0]};  // Bit_Extender bit_extender_4
  assign bit_extender_5_out = {{16{dataIn[15]}}, dataIn[15:0]};  // Bit_Extender bit_extender_5
  assign bit_extender_6_out = {{24{1'b0}}, dataIn[7:0]};  // Bit_Extender bit_extender_6
  assign bit_extender_7_out = {{16{1'b0}}, dataIn[15:0]};  // Bit_Extender bit_extender_7
  assign bit_extender_8_out = {{24{1'b0}}, stagereg_3_bdata};  // Bit_Extender bit_extender_8
  assign bit_extender_9_out = {{16{1'b0}}, {stagereg_3_bdata_2, stagereg_3_bdata}};  // Bit_Extender bit_extender_9
  Multiplexer #(.width(32)) multiplexer_11 (
    .in0(stagereg_3_opdata), .in1(multiplexer_12_out), .out(multiplexer_11_out), .sel(stagereg_3_writesmem));
  Register #(.trigger("low"), .width(32)) register_2 (
    .D(multiplexer_11_out), .Q(register_2_q), .clk(clock_1_out));  // open: en, clr
  and and_4 (write, stagereg_3_writesmem, not_4_out);
  not not_4 (not_4_out, clock_1_out);
  Multiplexer #(.select(3), .width(32)) multiplexer_12 (
    .in0(bit_extender_4_out), .in1(bit_extender_5_out), .in3(dataIn), .in4(bit_extender_6_out),
    .in5(bit_extender_7_out), .out(multiplexer_12_out), .sel(stagereg_3_opout[2:0]));  // open: in2, in6, in7
  Multiplexer #(.select(3), .width(32)) multiplexer_13 (
    .in0(bit_extender_8_out), .in1(bit_extender_9_out),
    .in3({stagereg_3_bdata_4, stagereg_3_bdata_3, stagereg_3_bdata_2, stagereg_3_bdata}), .out(dataOut),
    .sel(stagereg_3_opout[2:0]));  // open: in2, in4, in5, in6, in7
  or or_8 (or_8_out, write, read);
  and and_5 (read, stagereg_3_readsmem, not_4_out);
  stageReg stagereg_4 (
    .in_1(stagereg_3_opout), .in_2(stagereg_3_funcout), .in_3(stagereg_3_shout), .in_4(stagereg_3_trex),
    .in_5(stagereg_3_arex), .in_6(stagereg_3_brex), .in_7(stagereg_3_regstore), .in_8(stagereg_3_jump),
    .in_9(stagereg_3_branch), .in_10(stagereg_3_usesbrex), .in_11(stagereg_3_usesimm),
    .in_12(stagereg_3_writesmem), .in_13(stagereg_3_readsmem), .in_14(stagereg_3_aluop),
    .in_15(register_2_q), .in_16(stagereg_3_pcout), .in_17(stagereg_3_adata),
    .in_18({stagereg_3_bdata_4, stagereg_3_bdata_3, stagereg_3_bdata_2, stagereg_3_bdata}),
    .store(clock_1_out), .trex(stagereg_4_trex), .regStore(stagereg_4_regstore), .jump(stagereg_4_jump),
    .opData(stagereg_4_opdata), .pcOut(stagereg_4_pcout));  // open: flush, opOut, funcOut, shOut, arex, brex, branch, usesBRex, usesImm, writesMem, readsMem, aluOp, aData, bData
  and and_6 (and_6_out, stagereg_4_regstore, buffer_2_out);
  Multiplexer #(.width(32)) multiplexer_14 (
    .in0(stagereg_4_opdata), .in1(adder_3_out), .out(multiplexer_14_out), .sel(stagereg_4_jump));
  Adder #(.width(32)) adder_3 (.a(stagereg_4_pcout), .b(32'h4), .out(adder_3_out));  // open: cin, cout
  buf buffer_2 (buffer_2_out, buffer_3_out);
  buf buffer_3 (buffer_3_out, buffer_4_out);
  buf buffer_4 (buffer_4_out, buffer_5_out);
  buf buffer_5 (buffer_5_out, buffer_6_out);
  buf buffer_6 (buffer_6_out, buffer_7_out);
  buf buffer_7 (buffer_7_out, buffer_8_out);
  buf buffer_8 (buffer_8_out, buffer_9_out);
  buf buffer_9 (buffer_9_out, buffer_10_out);
  buf buffer_10 (buffer_10_out, not_4_out);
endmodule

module Regs (
  input  [4:0] in_1,
  input  [4:0] in_2,
  input  [4:0] in_3,
  input  [31:0] in_4,
  input  in_5,
  output [31:0] out_6,
  output [31:0] out_7
);

  wire decoder_1_out1, decoder_1_out2, decoder_1_out3, decoder_1_out4, decoder_1_out5, decoder_1_out6,
       decoder_1_out7, decoder_1_out8, decoder_1_out9, decoder_1_out10, decoder_1_out11, decoder_1_out12,
       decoder_1_out13, decoder_1_out14, decoder_1_out15, decoder_1_out16, decoder_1_out17, decoder_1_out18,
       decoder_1_out19, decoder_1_out20, decoder_1_out21, decoder_1_out22, decoder_1_out23, decoder_1_out24,
       decoder_1_out25, decoder_1_out26, decoder_1_out27, decoder_1_out28, decoder_1_out29, decoder_1_out30,
       decoder_1_out31;
  wire [31:0] pull_resistor_1_node, register_1_q, register_2_q, register_3_q, register_4_q, register_5_q,
       register_6_q, register_7_q, register_8_q, register_9_q, register_10_q, register_11_q, register_12_q,
       register_13_q, register_14_q, register_15_q, register_16_q, register_17_q, register_18_q,
       register_19_q, register_20_q, register_21_q, register_22_q, register_23_q, register_24_q,
       register_25_q, register_26_q, register_27_q, register_28_q, register_29_q, register_30_q,
       register_31_q;

  Decoder #(.select(5)) decoder_1 (
    .out1(decoder_1_out1), .out2(decoder_1_out2), .out3(decoder_1_out3), .out4(decoder_1_out4),
    .out5(decoder_1_out5), .out6(decoder_1_out6), .out7(decoder_1_out7), .out8(decoder_1_out8),
    .out9(decoder_1_out9), .out10(decoder_1_out10), .out11(decoder_1_out11), .out12(decoder_1_out12),
    .out13(decoder_1_out13), .out14(decoder_1_out14), .out15(decoder_1_out15), .out16(decoder_1_out16),
    .out17(decoder_1_out17), .out18(decoder_1_out18), .out19(decoder_1_out19), .out20(decoder_1_out20),
    .out21(decoder_1_out21), .out22(decoder_1_out22), .out23(decoder_1_out23), .out24(decoder_1_out24),
    .out25(decoder_1_out25), .out26(decoder_1_out26), .out27(decoder_1_out27), .out28(decoder_1_out28),
    .out29(decoder_1_out29), .out30(decoder_1_out30), .out31(decoder_1_out31), .sel(in_1), .en(in_5));  // open: out0
  Pull_Resistor pull_resistor_1 (.node(pull_resistor_1_node));
  Register #(.trigger("high"), .width(32)) register_1 (
    .D(in_4), .Q(register_1_q), .clk(decoder_1_out1));  // open: en, clr
  Register #(.trigger("high"), .width(32)) register_2 (
    .D(in_4), .Q(register_2_q), .clk(decoder_1_out2));  // open: en, clr
  Register #(.trigger("high"), .width(32)) register_3 (
    .D(in_4), .Q(register_3_q), .clk(decoder_1_out3));  // open: en, clr
  Register #(.trigger("high"), .width(32)) register_4 (
    .D(in_4), .Q(register_4_q), .clk(decoder_1_out4));  // open: en, clr
  Register #(.trigger("high"), .width(32)) register_5 (
    .D(in_4), .Q(register_5_q), .clk(decoder_1_out5));  // open: en, clr
  Register #(.trigger("high"), .width(32)) register_6 (
    .D(in_4), .Q(register_6_q), .clk(decoder_1_out6));  // open: en, clr
  Register #(.trigger("high"), .width(32)) register_7 (
    .D(in_4), .Q(register_7_q), .clk(decoder_1_out7));  // open: en, clr
  Register #(.trigger("high"), .width(32)) register_8 (
    .D(in_4), .Q(register_8_q), .clk(decoder_1_out8));  // open: en, clr
  Register #(.trigger("high"), .width(32)) register_9 (
    .D(in_4), .Q(register_9_q), .clk(decoder_1_out9));  // open: en, clr
  Register #(.trigger("high"), .width(32)) register_10 (
    .D(in_4), .Q(register_10_q), .clk(decoder_1_out10));  // open: en, clr
  Register #(.trigger("high"), .width(32)) register_11 (
    .D(in_4), .Q(register_11_q), .clk(decoder_1_out11));  // open: en, clr
  Register #(.trigger("high"), .width(32)) register_12 (
    .D(in_4), .Q(register_12_q), .clk(decoder_1_out12));  // open: en, clr
  Register #(.trigger("high"), .width(32)) register_13 (
    .D(in_4), .Q(register_13_q), .clk(decoder_1_out13));  // open: en, clr
  Register #(.trigger("high"), .width(32)) register_14 (
    .D(in_4), .Q(register_14_q), .clk(decoder_1_out14));  // open: en, clr
  Register #(.trigger("high"), .width(32)) register_15 (
    .D(in_4), .Q(register_15_q), .clk(decoder_1_out15));  // open: en, clr
  Register #(.trigger("high"), .width(32)) register_16 (
    .D(in_4), .Q(register_16_q), .clk(decoder_1_out16));  // open: en, clr
  Register #(.trigger("high"), .width(32)) register_17 (
    .D(in_4), .Q(register_17_q), .clk(decoder_1_out17));  // open: en, clr
  Register #(.trigger("high"), .width(32)) register_18 (
    .D(in_4), .Q(register_18_q), .clk(decoder_1_out18));  // open: en, clr
  Register #(.trigger("high"), .width(32)) register_19 (
    .D(in_4), .Q(register_19_q), .clk(decoder_1_out19));  // open: en, clr
  Register #(.trigger("high"), .width(32)) register_20 (
    .D(in_4), .Q(register_20_q), .clk(decoder_1_out20));  // open: en, clr
  Register #(.trigger("high"), .width(32)) register_21 (
    .D(in_4), .Q(register_21_q), .clk(decoder_1_out21));  // open: en, clr
  Register #(.trigger("high"), .width(32)) register_22 (
    .D(in_4), .Q(register_22_q), .clk(decoder_1_out22));  // open: en, clr
  Register #(.trigger("high"), .width(32)) register_23 (
    .D(in_4), .Q(register_23_q), .clk(decoder_1_out23));  // open: en, clr
  Register #(.trigger("high"), .width(32)) register_24 (
    .D(in_4), .Q(register_24_q), .clk(decoder_1_out24));  // open: en, clr
  Register #(.trigger("high"), .width(32)) register_25 (
    .D(in_4), .Q(register_25_q), .clk(decoder_1_out25));  // open: en, clr
  Register #(.trigger("high"), .width(32)) register_26 (
    .D(in_4), .Q(register_26_q), .clk(decoder_1_out26));  // open: en, clr
  Register #(.trigger("high"), .width(32)) register_27 (
    .D(in_4), .Q(register_27_q), .clk(decoder_1_out27));  // open: en, clr
  Register #(.trigger("high"), .width(32)) register_28 (
    .D(in_4), .Q(register_28_q), .clk(decoder_1_out28));  // open: en, clr
  Register #(.trigger("high"), .width(32)) register_29 (
    .D(in_4), .Q(register_29_q), .clk(decoder_1_out29));  // open: en, clr
  Register #(.trigger("high"), .width(32)) register_30 (
    .D(in_4), .Q(register_30_q), .clk(decoder_1_out30));  // open: en, clr
  Register #(.trigger("high"), .width(32)) register_31 (
    .D(in_4), .Q(register_31_q), .clk(decoder_1_out31));  // open: en, clr
  Multiplexer #(.select(5), .width(32)) multiplexer_1 (
    .in0(pull_resistor_1_node), .in1(register_1_q), .in2(register_2_q), .in3(register_3_q),
    .in4(register_4_q), .in5(register_5_q), .in6(register_6_q), .in7(register_7_q), .in8(register_8_q),
    .in9(register_9_q), .in10(register_10_q), .in11(register_11_q), .in12(register_12_q),
    .in13(register_13_q), .in14(register_14_q), .in15(register_15_q), .in16(register_16_q),
    .in17(register_17_q), .in18(register_18_q), .in19(register_19_q), .in20(register_20_q),
    .in21(register_21_q), .in22(register_22_q), .in23(register_23_q), .in24(register_24_q),
    .in25(register_25_q), .in26(register_26_q), .in27(register_27_q), .in28(register_28_q),
    .in29(register_29_q), .in30(register_30_q), .in31(register_31_q), .out(out_6), .sel(in_2));
  Multiplexer #(.select(5), .width(32)) multiplexer_2 (
    .in0(pull_resistor_1_node), .in1(register_1_q), .in2(register_2_q), .in3(register_3_q),
    .in4(register_4_q), .in5(register_5_q), .in6(register_6_q), .in7(register_7_q), .in8(register_8_q),
    .in9(register_9_q), .in10(register_10_q), .in11(register_11_q), .in12(register_12_q),
    .in13(register_13_q), .in14(register_14_q), .in15(register_15_q), .in16(register_16_q),
    .in17(register_17_q), .in18(register_18_q), .in19(register_19_q), .in20(register_20_q),
    .in21(register_21_q), .in22(register_22_q), .in23(register_23_q), .in24(register_24_q),
    .in25(register_25_q), .in26(register_26_q), .in27(register_27_q), .in28(register_28_q),
    .in29(register_29_q), .in30(register_30_q), .in31(register_31_q), .out(out_7), .sel(in_3));
endmodule

module alu (
  input  [31:0] in_1,
  input  [31:0] in_2,
  input  [5:0] in_3,
  input  [4:0] in_4,
  input  in_5,
  output [31:0] out_6,
  output out_7,
  output out_8
);

  wire adder_1_cout, and_1_out, and_2_out, and_6_out, and_7_out, and_8_out, and_9_out, and_10_out,
       and_11_out, comparator_1_lt, comparator_2_lt, subtractor_1_bout;
  wire [4:0] bit_extender_1_out, multiplexer_1_out;
  wire [31:0] adder_1_out, and_5_out, bit_extender_2_out, bit_extender_3_out, controlled_buffer_1_out,
       controlled_buffer_2_out, divider_1_out, divider_1_rem, divider_2_out, divider_2_rem, hi_q, lo_q,
       multiplexer_2_out, multiplexer_3_out, multiplexer_4_out, multiplexer_5_out, multiplier_1_cout,
       multiplier_1_out, multiplier_2_cout, multiplier_2_out, nor_1_out, or_1_out, or_2_out, or_3_out,
       pull_resistor_1_node, pull_resistor_2_node, shifter_1_out, shifter_2_out, shifter_3_out,
       subtractor_1_out, xor_1_out;

  and and_1 (and_1_out, ~in_3[0], ~in_3[1], ~in_3[2]);  // AND_Gate
  and and_2 (and_2_out, in_3[0], ~in_3[1], in_3[2]);  // AND_Gate
  and and_3 (out_8, subtractor_1_bout, and_1_out);
  and and_4 (out_7, adder_1_cout, and_2_out);
  Multiplexer #(.width(5)) multiplexer_1 (.in0(in_4), .in1(bit_extender_1_out), .out(multiplexer_1_out), .sel(in_3[2]));
  Bit_Extender #(.in_width(32), .out_width(5)) bit_extender_1 (.in(in_1), .out(bit_extender_1_out));
  Shifter #(.width(32)) shifter_1 (.in(in_2), .\dist (multiplexer_1_out), .out(shifter_1_out));
  Shifter #(.shift("lr"), .width(32)) shifter_2 (.in(in_2), .\dist (multiplexer_1_out), .out(shifter_2_out));
  Shifter #(.shift("ar"), .width(32)) shifter_3 (.in(in_2), .\dist (multiplexer_1_out), .out(shifter_3_out));
  Multiplier #(.mode("twosComplement"), .width(32)) multiplier_1 (
    .a(in_1), .b(in_2), .out(multiplier_1_out), .cout(multiplier_1_cout));  // open: cin
  Divider #(.mode("twosComplement"), .width(32)) divider_1 (
    .a(in_1), .b(in_2), .out(divider_1_out), .rem(divider_1_rem));  // open: upper
  Multiplier #(.width(32)) multiplier_2 (
    .a(in_1), .b(in_2), .out(multiplier_2_out), .cout(multiplier_2_cout));  // open: cin
  Divider #(.width(32)) divider_2 (.a(in_1), .b(in_2), .out(divider_2_out), .rem(divider_2_rem));  // open: upper
  Adder #(.width(32)) adder_1 (.a(in_1), .b(in_2), .out(adder_1_out), .cout(adder_1_cout));  // open: cin
  Subtractor #(.width(32)) subtractor_1 (
    .a(in_1), .b(in_2), .out(subtractor_1_out), .bout(subtractor_1_bout));  // open: bin
  assign and_5_out = in_1 & in_2;  // AND_Gate and_5, 32 bits wide
  assign or_1_out = in_1 | in_2;  // OR_Gate or_1, 32 bits wide
  assign xor_1_out = in_1 ^ in_2;  // XOR_Gate xor_1, 32 bits wide
  assign nor_1_out = ~(in_1 | in_2);  // NOR_Gate nor_1, 32 bits wide
  Comparator #(.width(32)) comparator_1 (.a(in_1), .b(in_2), .lt(comparator_1_lt));  // open: gt, eq
  Comparator #(.mode("unsigned"), .width(32)) comparator_2 (.a(in_1), .b(in_2), .lt(comparator_2_lt));  // open: gt, eq
  Multiplexer #(.select(2), .width(32)) multiplexer_2 (
    .in0(shifter_1_out), .in2(shifter_2_out), .in3(shifter_3_out), .out(multiplexer_2_out), .sel(in_3[1:0]));  // open: in1
  Multiplexer #(.select(2), .width(32)) multiplexer_3 (
    .in0(multiplier_1_out), .in1(divider_1_out), .in2(multiplier_2_out), .in3(divider_2_out),
    .out(multiplexer_3_out), .sel(in_3[1:0]));
  Multiplexer #(.select(2), .width(32)) multiplexer_4 (
    .in0(multiplier_1_cout), .in1(divider_1_rem), .in2(multiplier_2_cout), .in3(divider_2_rem),
    .out(multiplexer_4_out), .sel(in_3[1:0]));
  Multiplexer #(.select(3), .width(32)) multiplexer_5 (
    .in0(adder_1_out), .in1(adder_1_out), .in2(subtractor_1_out), .in3(subtractor_1_out), .in4(and_5_out),
    .in5(or_1_out), .in6(xor_1_out), .in7(nor_1_out), .out(multiplexer_5_out), .sel(in_3[2:0]));
  and and_6 (and_6_out, ~in_3[2], in_3[1], ~in_3[0]);  // AND_Gate
  assign bit_extender_2_out = {{31{1'b0}}, comparator_1_lt};  // Bit_Extender bit_extender_2
  assign bit_extender_3_out = {{31{1'b0}}, comparator_2_lt};  // Bit_Extender bit_extender_3
  and and_7 (and_7_out, and_8_out, in_5);
  and and_8 (and_8_out, ~in_3[5], in_3[4], in_3[3]);  // AND_Gate
  and and_9 (and_9_out, ~in_3[2], in_3[1], in_3[0]);  // AND_Gate
  assign controlled_buffer_1_out = and_6_out ? bit_extender_2_out : 32'bz;  // Controlled_Buffer controlled_buffer_1
  assign controlled_buffer_2_out = and_9_out ? bit_extender_3_out : 32'bz;  // Controlled_Buffer controlled_buffer_2
  Pull_Resistor pull_resistor_1 (.node(pull_resistor_1_node));
  assign pull_resistor_1_node = and_11_out ? lo_q : 32'bz;  // Controlled_Buffer controlled_buffer_3
  Register #(.trigger("falling"), .width(32)) lo (.D(multiplexer_3_out), .Q(lo_q), .clk(and_7_out));  // open: en, clr
  Pull_Resistor pull_resistor_2 (.node(pull_resistor_2_node));
  assign pull_resistor_2_node = and_10_out ? hi_q : 32'bz;  // Controlled_Buffer controlled_buffer_4
  Register #(.trigger("falling"), .width(32)) hi (.D(multiplexer_4_out), .Q(hi_q), .clk(and_7_out));  // open: en, clr
  and and_10 (and_10_out, ~in_3[2], ~in_3[1], ~in_3[0]);  // AND_Gate
  and and_11 (and_11_out, ~in_3[2], in_3[1], ~in_3[0]);  // AND_Gate
  Pull_Resistor pull_resistor_3 (.node(controlled_buffer_1_out));
  assign or_2_out = controlled_buffer_1_out | controlled_buffer_2_out;  // OR_Gate or_2, 32 bits wide
  Pull_Resistor pull_resistor_4 (.node(controlled_buffer_2_out));
  assign or_3_out = pull_resistor_1_node | pull_resistor_2_node;  // OR_Gate or_3, 32 bits wide
  Multiplexer #(.select(3), .width(32)) multiplexer_6 (
    .in0(multiplexer_2_out), .in2(or_3_out), .in4(multiplexer_5_out), .in5(or_2_out), .out(out_6),
    .sel(in_3[5:3]));  // open: in1, in3, in6, in7
endmodule

module idk (
  input  [5:0] in_1,
  input  [4:0] in_2,
  input  [4:0] in_3,
  input  [4:0] in_4,
  input  [4:0] in_5,
  input  [5:0] in_6
);

  wire button_1_out, ram_1_p1, ram_1_p2;

  // Probe on in_6
  // Probe on {in_6, in_5, in_4, in_3, in_2, in_1}
  Button button_1 (.out(button_1_out));
  // RAM #(.addrWidth(2), .enables("line"), .line("quad"), .misaligned("true"), .\type ("nonvolatile")) ram_1: pin names not known; wires that end beside it: ram_1_p1, ram_1_p2, button_1_out, {in_2[1:0], in_1}, {in_3, in_2[4:2]}, {in_5[2:0], in_4}, {in_6, in_5[4:3]}
  Pull_Resistor pull_resistor_1 (.node(ram_1_p1));
  Pull_Resistor #(.pull(1)) pull_resistor_2 (.node(ram_1_p2));
endmodule

module hazUnit (
  input  [4:0] in_1,
  input  [4:0] in_2,
  input  [5:0] in_3
);

  wire or_1_out;

  Multiplexer #(.width(5)) multiplexer_1 (.in0(in_1), .in1(in_2), .sel(or_1_out));  // open: out
  or or_1 (or_1_out, in_3[5], in_3[4], in_3[3], in_3[2], in_3[1], in_3[0]);
endmodule

module decoderer (
  input  [5:0] func,
  input  [4:0] sh,
  input  [4:0] rd,
  input  [4:0] rt,
  input  [4:0] rs,
  input  [5:0] op,
  input  [15:0] imm16,
  input  [25:0] imm26,
  input  [31:0] pc,
  input  cancelInst,
  output [5:0] opOut,
  output [5:0] funcOut,
  output [4:0] shOut,
  output [4:0] trex,
  output [4:0] arex,
  output [4:0] brex,
  output regStore,
  output jump,
  output branch,
  output usesBRex,
  output usesImm,
  output writesMem,
  output readsMem,
  output aluOp,
  output [31:0] imm,
  output [31:0] pcOut
);

  wire and_1_out, and_2_out, not_1_out, not_2_out;
  wire [4:0] multiplexer_2_out, multiplexer_3_out;
  wire [5:0] multiplexer_4_out;
  wire [5:3] and_3_out;
  wire [10:0] funcdec_1_out_2, multiplexer_6_out, pla_1_out;
  wire [31:0] bit_extender_1_out, bit_extender_2_out, bit_extender_3_out, multiplexer_1_out,
       multiplexer_5_out, shifter_1_out;

  and and_1 (and_1_out, ~op[5], ~op[4], op[3]);  // AND_Gate
  and and_2 (and_2_out, ~op[5], ~op[4], op[3], op[2], op[1], op[0]);  // AND_Gate
  assign bit_extender_1_out = {{16{imm16[15]}}, imm16};  // Bit_Extender bit_extender_1
  Multiplexer #(.width(32)) multiplexer_1 (
    .in0(bit_extender_1_out), .in1(bit_extender_2_out), .out(multiplexer_1_out), .sel(multiplexer_6_out[1]));
  assign bit_extender_2_out = {{16{1'b0}}, imm16};  // Bit_Extender bit_extender_2
  assign bit_extender_3_out = {{6{imm26[25]}}, imm26};  // Bit_Extender bit_extender_3
  Multiplexer #(.width(5)) multiplexer_2 (.in0(rd), .in1(rt), .out(multiplexer_2_out), .sel(not_1_out));
  not not_1 (not_1_out, multiplexer_6_out[6]);
  Pull_Resistor #(.pull(1)) pull_resistor_1 (.node(and_3_out[5]));
  Pull_Resistor pull_resistor_2 (.node(and_3_out[4]));
  and and_3 (and_3_out[3], ~op[2], op[1]);  // AND_Gate
  Shifter #(.width(32)) shifter_1 (.in(multiplexer_1_out), .\dist (multiplexer_3_out), .out(shifter_1_out));
  Multiplexer #(.width(5)) multiplexer_3 (.in0({5{1'b0}}), .in1(5'b10000), .out(multiplexer_3_out), .sel(and_2_out));
  Multiplexer #(.width(6)) multiplexer_4 (
    .in0(func), .in1({and_3_out, op[2:0]}), .out(multiplexer_4_out), .sel(and_1_out));
  PLA #(.in_width(6), .out_width(11), .\table ("000000 00001000001\n000010 00010010100\n000011 00010011000\n0001xx 00010110000\n0010xx 10010001000\n0011xx 10010001010\n100xxx 00110001000\n101xxx 01010000000")) pla_1 (
    .in(op), .out(pla_1_out));
  Multiplexer #(.width(32)) multiplexer_5 (
    .in0(shifter_1_out), .in1(bit_extender_3_out), .out(multiplexer_5_out), .sel(multiplexer_6_out[2]));
  funcDec funcdec_1 (.in_1(op), .out_2(funcdec_1_out_2));
  Multiplexer #(.width(11)) multiplexer_6 (
    .in0(pla_1_out), .in1(funcdec_1_out_2), .out(multiplexer_6_out), .sel(pla_1_out[0]));
  Pull_Resistor pull_resistor_3 (.node(opOut));
  assign opOut = not_2_out ? op : 6'bz;  // Controlled_Buffer controlled_buffer_1
  Pull_Resistor pull_resistor_4 (.node(funcOut));
  assign funcOut = not_2_out ? multiplexer_4_out : 6'bz;  // Controlled_Buffer controlled_buffer_2
  Pull_Resistor pull_resistor_5 (.node(shOut));
  assign shOut = not_2_out ? sh : 5'bz;  // Controlled_Buffer controlled_buffer_3
  Pull_Resistor pull_resistor_6 (.node(trex));
  assign trex = not_2_out ? multiplexer_2_out : 5'bz;  // Controlled_Buffer controlled_buffer_4
  Pull_Resistor pull_resistor_7 (.node(arex));
  assign arex = not_2_out ? rs : 5'bz;  // Controlled_Buffer controlled_buffer_5
  Pull_Resistor pull_resistor_8 (.node(brex));
  assign brex = not_2_out ? rt : 5'bz;  // Controlled_Buffer controlled_buffer_6
  Pull_Resistor pull_resistor_9 (.node(regStore));
  assign regStore = not_2_out ? multiplexer_6_out[3] : 1'bz;  // Controlled_Buffer controlled_buffer_7
  Pull_Resistor pull_resistor_10 (.node(jump));
  assign jump = not_2_out ? multiplexer_6_out[4] : 1'bz;  // Controlled_Buffer controlled_buffer_8
  Pull_Resistor pull_resistor_11 (.node(branch));
  assign branch = not_2_out ? multiplexer_6_out[5] : 1'bz;  // Controlled_Buffer controlled_buffer_9
  Pull_Resistor pull_resistor_12 (.node(usesBRex));
  assign usesBRex = not_2_out ? multiplexer_6_out[6] : 1'bz;  // Controlled_Buffer controlled_buffer_10
  Pull_Resistor pull_resistor_13 (.node(usesImm));
  assign usesImm = not_2_out ? multiplexer_6_out[7] : 1'bz;  // Controlled_Buffer controlled_buffer_11
  Pull_Resistor pull_resistor_14 (.node(writesMem));
  assign writesMem = not_2_out ? multiplexer_6_out[8] : 1'bz;  // Controlled_Buffer controlled_buffer_12
  Pull_Resistor pull_resistor_15 (.node(readsMem));
  assign readsMem = not_2_out ? multiplexer_6_out[9] : 1'bz;  // Controlled_Buffer controlled_buffer_13
  Pull_Resistor pull_resistor_16 (.node(aluOp));
  assign aluOp = not_2_out ? multiplexer_6_out[10] : 1'bz;  // Controlled_Buffer controlled_buffer_14
  Pull_Resistor pull_resistor_17 (.node(imm));
  assign imm = not_2_out ? multiplexer_5_out : 32'bz;  // Controlled_Buffer controlled_buffer_15
  Pull_Resistor pull_resistor_18 (.node(pcOut));
  assign pcOut = not_2_out ? pc : 32'bz;  // Controlled_Buffer controlled_buffer_16
  not not_2 (not_2_out, cancelInst);
endmodule

module stageReg (
  input  [5:0] in_1,
  input  [5:0] in_2,
  input  [4:0] in_3,
  input  [4:0] in_4,
  input  [4:0] in_5,
  input  [4:0] in_6,
  input  in_7,
  input  in_8,
  input  in_9,
  input  in_10,
  input  in_11,
  input  in_12,
  input  in_13,
  input  in_14,
  input  [31:0] in_15,
  input  [31:0] in_16,
  input  [31:0] in_17,
  input  [31:0] in_18,
  input  store,
  input  flush,
  output [5:0] opOut,
  output [5:0] funcOut,
  output [4:0] shOut,
  output [4:0] trex,
  output [4:0] arex,
  output [4:0] brex,
  output regStore,
  output jump,
  output branch,
  output usesBRex,
  output usesImm,
  output writesMem,
  output readsMem,
  output aluOp,
  output [31:0] opData,
  output [31:0] pcOut,
  output [31:0] aData,
  output [31:0] bData
);

  Register #(.trigger("falling"), .width(6)) register_1 (.D(in_1), .Q(opOut), .clk(store), .clr(flush));  // open: en
  Register #(.trigger("falling"), .width(6)) register_2 (.D(in_2), .Q(funcOut), .clk(store), .clr(flush));  // open: en
  Register #(.trigger("falling"), .width(5)) register_3 (.D(in_3), .Q(shOut), .clk(store), .clr(flush));  // open: en
  Register #(.trigger("falling"), .width(5)) register_4 (.D(in_4), .Q(trex), .clk(store), .clr(flush));  // open: en
  Register #(.trigger("falling"), .width(5)) register_5 (.D(in_5), .Q(arex), .clk(store), .clr(flush));  // open: en
  Register #(.trigger("falling"), .width(5)) register_6 (.D(in_6), .Q(brex), .clk(store), .clr(flush));  // open: en
  Register #(.trigger("falling"), .width(1)) register_7 (.D(in_7), .Q(regStore), .clk(store), .clr(flush));  // open: en
  Register #(.trigger("falling"), .width(1)) register_8 (.D(in_8), .Q(jump), .clk(store), .clr(flush));  // open: en
  Register #(.trigger("falling"), .width(1)) register_9 (.D(in_9), .Q(branch), .clk(store), .clr(flush));  // open: en
  Register #(.trigger("falling"), .width(1)) register_10 (
    .D(in_10), .Q(usesBRex), .clk(store), .clr(flush));  // open: en
  Register #(.trigger("falling"), .width(1)) register_11 (
    .D(in_11), .Q(usesImm), .clk(store), .clr(flush));  // open: en
  Register #(.trigger("falling"), .width(1)) register_12 (
    .D(in_12), .Q(writesMem), .clk(store), .clr(flush));  // open: en
  Register #(.trigger("falling"), .width(1)) register_13 (
    .D(in_13), .Q(readsMem), .clk(store), .clr(flush));  // open: en
  Register #(.trigger("falling"), .width(1)) register_14 (.D(in_14), .Q(aluOp), .clk(store), .clr(flush));  // open: en
  Register #(.trigger("falling"), .width(32)) register_15 (
    .D(in_15), .Q(opData), .clk(store), .clr(flush));  // open: en
  Register #(.trigger("falling"), .width(32)) register_16 (.D(in_16), .Q(pcOut), .clk(store), .clr(flush));  // open: en
  Register #(.trigger("falling"), .width(32)) register_17 (.D(in_17), .Q(aData), .clk(store), .clr(flush));  // open: en
  Register #(.trigger("falling"), .width(32)) register_18 (.D(in_18), .Q(bData), .clk(store), .clr(flush));  // open: en
endmodule

module forwarding_unit (
  input  [4:0] s,
  input  [4:0] t1,
  input  [4:0] t2,
  input  in_4,
  output [1:0] out_5
);

  wire and_1_out, comparator_1_eq, comparator_2_eq;
  wire [1:0] comparator_3_eq;
  wire [4:0] pull_resistor_2_node;

  Pull_Resistor pull_resistor_1 (.node(out_5));
  Comparator #(.width(5)) comparator_1 (.a(s), .b(pull_resistor_2_node), .eq(comparator_1_eq));  // open: gt, lt
  Pull_Resistor pull_resistor_2 (.node(pull_resistor_2_node));
  and and_1 (and_1_out, ~comparator_1_eq, in_4);  // AND_Gate
  assign out_5 = and_1_out ? comparator_3_eq : 2'bz;  // Controlled_Buffer controlled_buffer_1
  Comparator #(.width(5)) comparator_2 (.a(t2), .b(s), .eq(comparator_2_eq));  // open: gt, lt
  Comparator #(.width(5)) comparator_3 (.a(t1), .b(s), .eq(comparator_3_eq[0]));  // open: gt, lt
  and and_2 (comparator_3_eq[1], comparator_2_eq, ~comparator_3_eq[0]);  // AND_Gate
endmodule

module plas (
);

  // PlaRom #(.Contents("1*10 2 1*5 2 2 1*3 2 0 0 1 1 2 0*3 2 1 1 0*3 2 1 2 0*3 0*3 1 0*5 1 0 0 1 0 0 1 0 1 0*4 1 0 0 1*3 0*4 1 0 1 0*3 1 0*3 1 0*3 1 0 1 0 0 1 1 0*3 1 0 1 0 1 0 1 0*5 1 0"), .\and (7), .outputs(10)) plarom_1: pin names not known
  // PlaRom #(.Contents("1 1 2 1*5 2 1 1 2 0 1 0*4 2*6 0*3 1 0 1 0*3 1 0*3 1 0 1 1 0 0 1 0*3 1 0 0 1 0 0 1*11"), .outputs(10)) plarom_2: pin names not known
endmodule

module funcDec (
  input  [5:0] in_1,
  output [10:0] out_2
);

  wire and_1_out, not_1_out, not_2_out, not_3_out, not_4_out, not_5_out, not_6_out;

  not not_1 (not_1_out, in_1[5]);
  not not_2 (not_2_out, in_1[4]);
  not not_3 (not_3_out, in_1[3]);
  not not_4 (not_4_out, in_1[2]);
  not not_5 (not_5_out, in_1[1]);
  not not_6 (not_6_out, in_1[0]);
  and and_1 (and_1_out, not_6_out, not_5_out, not_4_out, in_1[3], not_2_out, not_1_out);
  not not_7 (out_2[3], and_1_out);
  not not_8 (out_2[10], in_1[3]);
  Pull_Resistor pull_resistor_1 (.node({out_2[10:5], in_1[3], out_2[3:0]}));

  assign out_2[4] = in_1[3];
  // also tied to VCC on the sheet: {out_2[0], out_2[6]}
endmodule

module forwarding_unit_big (
  input  [4:0] s,
  input  [4:0] t1,
  input  [4:0] t2,
  input  [4:0] t3,
  input  in_5,
  output [1:0] out_6
);

  wire and_1_out, comparator_1_eq, comparator_2_eq, comparator_3_eq, comparator_4_eq;
  wire [1:0] priority_encoder_1_out;
  wire [4:0] pull_resistor_2_node;

  Pull_Resistor pull_resistor_1 (.node(out_6));
  Comparator #(.width(5)) comparator_1 (.a(s), .b(pull_resistor_2_node), .eq(comparator_1_eq));  // open: gt, lt
  Pull_Resistor pull_resistor_2 (.node(pull_resistor_2_node));
  and and_1 (and_1_out, ~comparator_1_eq, in_5);  // AND_Gate
  assign out_6 = and_1_out ? priority_encoder_1_out : 2'bz;  // Controlled_Buffer controlled_buffer_1
  Comparator #(.width(5)) comparator_2 (.a(t3), .b(s), .eq(comparator_2_eq));  // open: gt, lt
  Comparator #(.width(5)) comparator_3 (.a(t2), .b(s), .eq(comparator_3_eq));  // open: gt, lt
  Comparator #(.width(5)) comparator_4 (.a(t1), .b(s), .eq(comparator_4_eq));  // open: gt, lt
  Priority_Encoder #(.select(2)) priority_encoder_1 (
    .in1(comparator_2_eq), .in2(comparator_3_eq), .in3(comparator_4_eq), .out(priority_encoder_1_out));  // open: in0, gs, en_out, en_in
endmodule
